# Fritzing sketch minno-perf (saved by Fritzing 0.9.2b)
breadboards: 1

parts:
  Part1 = Arduino Leonardo (Rev3b)
  S1 = Toggle Switch [package=THT]
  R3 = Resistor [tolerance=±5% resistance=10k package=THT]
  R2 = Resistor [tolerance=±5% resistance=10k package="2010 [SMD]"]
  P1 = S1133 Si Photodiode [package="8mm Ceramic [THT]"]

nets:
  N1: Part1.D0/RX, R3.Pin_1, P1.cathode
  N2: Part1.D4/A6, S1.L2, R2.Pin_1
  N3: Part1.5V, R2.Pin_0, P1.anode
  N4: Part1.GND, S1.COM, R3.Pin_0
